# Fritzing sketch pyro-receiver (saved by Fritzing 1.0.4)
circuit board: 4.91115cm x 4.91897cm
perfboards: 1

parts:
  Part1 = Arduino Nano (Rev3.0)
  M1 = Osoyoo SX1278-ra-02
  LED2 = LED - 3mm [color="Red (633nm)" current=30mA package="3 mm [THT]"]
  R1 = Resistor [tolerance=±5% power=0.25W resistance=220 package=THT]

nets:
  GND: Part1.GND, M1.GND, LED2.anode
  N1: Part1.D2, M1.DIO0
  N2: Part1.D8, R1.Pin_0
  N3: Part1.D9, M1.RST
  N4: Part1.D10, M1.NSS
  N5: Part1.D11/MOSI, M1.MOSI
  N6: Part1.D12/MISO, M1.MISO
  3V3: Part1.3V3, M1.3.3V
  N7: Part1.D13/SCK, M1.SCK
  N8: LED2.cathode, R1.Pin_1

custom parts:
  Osoyoo SX1278-ra-02: Osoyoo Long Distance wireless transceiver Uart LoRa Module.
